# Fritzing sketch Exo1 (saved by Fritzing 0.9.3b)
breadboards: 1

parts:
  Composant1 = Arduino Mega 2560 (Rev3)
  R1 = Resistor [tolerance=±5% resistance=220 package=THT]
  R2 = Resistor [tolerance=±5% resistance=220 package=THT]
  R3 = Resistor [tolerance=±5% resistance=220 package=THT]
  R4 = Resistor [tolerance=±5% resistance=220 package=THT]
  R5 = Resistor [tolerance=±5% resistance=220 package=THT]
  R6 = Resistor [tolerance=±5% resistance=220 package=THT]
  R7 = Resistor [tolerance=±5% resistance=220 package=THT]
  R8 = Resistor [tolerance=±5% resistance=220 package=THT]
  R9 = Resistor [tolerance=±5% resistance=220 package=THT]
  R10 = Resistor [tolerance=±5% resistance=220 package=THT]
  LED1 = LED - 5mm [color="Red (633nm)" package="5 mm [THT]"]
  LED2 = LED - 5mm [color="Red (633nm)" package="5 mm [THT]"]
  LED3 = LED - 5mm [color="Red (633nm)" package="5 mm [THT]"]
  LED4 = LED - 5mm [color="Red (633nm)" package="5 mm [THT]"]
  LED5 = LED - 5mm [color="Red (633nm)" package="5 mm [THT]"]
  LED6 = LED - 5mm [color="Red (633nm)" package="5 mm [THT]"]
  LED7 = LED - 5mm [color="Red (633nm)" package="5 mm [THT]"]
  LED8 = LED - 5mm [color="Red (633nm)" package="5 mm [THT]"]
  LED9 = LED - 5mm [color="Red (633nm)" package="5 mm [THT]"]
  LED10 = LED - 5mm [color="Red (633nm)" package="5 mm [THT]"]
  Start = Pushbutton [package="[THT]"]
  Stop = Pushbutton [package="[THT]"]
  R11 = Resistor [tolerance=±5% resistance=220 package=THT]
  R12 = Resistor [tolerance=±5% resistance=220 package=THT]

nets:
  N1: Composant1.D13_PWM, R1.Pin_1, LED1.anode
  N2: Composant1.D12_PWM, R2.Pin_1, LED2.anode
  N3: Composant1.D11_PWM, R3.Pin_1, LED3.anode
  N4: Composant1.D10_PWM, R4.Pin_1, LED4.anode
  N5: Composant1.D9_PWM, R5.Pin_1, LED5.anode
  N6: Composant1.D8_PWM, R6.Pin_1, LED6.anode
  N7: Composant1.D2_PWM, Composant1.D3_PWM, LED1.cathode, LED2.cathode, LED3.cathode, LED4.cathode, LED5.cathode, LED6.cathode, LED7.cathode, LED8.cathode, LED9.cathode, LED10.cathode, Start.Pin_1, Start.Pin_2, Start.Pin_3, Start.Pin_4, Stop.Pin_1, Stop.Pin_2, Stop.Pin_3, Stop.Pin_4, R11.Pin_1, R12.Pin_1
  N8: Composant1.D4_PWM, R10.Pin_1, LED10.anode
  N9: Composant1.D5_PWM, R9.Pin_1, LED9.anode
  N10: Composant1.D6_PWM, R8.Pin_1, LED8.anode
  N11: Composant1.D7_PWM, R7.Pin_1, LED7.anode
  N12: R1.Pin_0, R2.Pin_0, R3.Pin_0, R4.Pin_0, R5.Pin_0, R6.Pin_0, R7.Pin_0, R8.Pin_0, R9.Pin_0, R10.Pin_0, R11.Pin_0, R12.Pin_0
