# Fritzing sketch Exo2 (saved by Fritzing 0.9.3b)
breadboards: 1

parts:
  Composant1 = Arduino Mega 2560 (Rev3)
  R1 = Resistor [tolerance=±5% resistance=220 package=THT]
  R3 = Resistor [tolerance=±5% resistance=220 package=THT]
  R4 = Resistor [tolerance=±5% resistance=220 package=THT]
  R5 = Resistor [tolerance=±5% resistance=220 package=THT]
  R6 = Resistor [tolerance=±5% resistance=220 package=THT]
  R7 = Resistor [tolerance=±5% resistance=220 package=THT]
  R8 = Resistor [tolerance=±5% resistance=220 package=THT]
  R10 = Resistor [tolerance=±5% resistance=220 package=THT]
  LED3 = LED - 5mm [color="Red (633nm)" package="5 mm [THT]"]
  LED4 = LED - 5mm [color="Red (633nm)" package="5 mm [THT]"]
  LED5 = LED - 5mm [color="Red (633nm)" package="5 mm [THT]"]
  LED6 = LED - 5mm [color="Red (633nm)" package="5 mm [THT]"]
  LED7 = LED - 5mm [color="Red (633nm)" package="5 mm [THT]"]
  b = Pushbutton [package="[THT]"]
  a = Pushbutton [package="[THT]"]
  Red_(633nm)_LED = LED - 5mm [color="Red (633nm)" package="5 mm [THT]"]

nets:
  N1: Composant1.D13_PWM, R3.Pin_1, LED3.anode
  N2: Composant1.D12_PWM, R4.Pin_1, LED4.anode
  N3: Composant1.D11_PWM, R5.Pin_1, LED5.anode
  N4: Composant1.D10_PWM, R6.Pin_1, LED6.anode
  N5: Composant1.D9_PWM, R7.Pin_1, LED7.anode
  N6: Composant1.D8_PWM, R8.Pin_1, Red_(633nm)_LED.anode
  N7: Composant1.5V, R1.Pin_0, R3.Pin_0, R4.Pin_0, R5.Pin_0, R6.Pin_0, R7.Pin_0, R8.Pin_0, R10.Pin_0
  N8: Composant1.GND, LED5.cathode, LED6.cathode, LED7.cathode, b.Pin_1, b.Pin_2, a.Pin_3, a.Pin_4, Red_(633nm)_LED.cathode
  N9: Composant1.D2_PWM, R10.Pin_1, b.Pin_3, b.Pin_4
  N10: Composant1.D3_PWM, R1.Pin_1, a.Pin_1, a.Pin_2
