# Fritzing sketch Exo4 (saved by Fritzing 0.9.3b)
circuit board: 8.46667cm x 5.64444cm
breadboards: 1

parts:
  l2C = LCM1602 IIC [part_number="LCM1602 IIC" chip_label="LCM1602 IIC" package="DIP (Dual Inline) [THT]"]
  Ecran_LCD = LCD screen
  Composant1 = Arduino Mega 2560 (Rev3)
  RTC_Module = Real Time Clock Module - DS1307 RTC Breakout Board

nets:
  VSS: l2C.VSS, Ecran_LCD.VSS
  VDD: l2C.VDD, Ecran_LCD.VDD
  N1: l2C.V0, Ecran_LCD.V0
  N2: l2C.RS, Ecran_LCD.RS
  N3: l2C.RW, Ecran_LCD.R/W
  N4: l2C.E, Ecran_LCD.E
  N5: l2C.D0, Ecran_LCD.DB0
  N6: l2C.D1, Ecran_LCD.DB1
  N7: l2C.D2, Ecran_LCD.DB2
  N8: l2C.D3, Ecran_LCD.DB3
  N9: l2C.D4, Ecran_LCD.DB4
  N10: l2C.D5, Ecran_LCD.DB5
  N11: l2C.D6, Ecran_LCD.DB6
  N12: l2C.D7, Ecran_LCD.DB7
  N13: l2C.A, Ecran_LCD.LED+
  N14: l2C.K, Ecran_LCD.LED-
  GND: l2C.GND, Composant1.GND, RTC_Module.GND
  5V: l2C.VCC, Composant1.5V, RTC_Module.5V
  N15: l2C.SDA, Composant1.D20/SDA, RTC_Module.SDA
  N16: l2C.SCL, Composant1.D21/SCL, RTC_Module.SCL
  N17: l2C.LED_A, l2C.LED_B

custom parts:
  LCM1602 IIC: I2C-Module to use a 1602 or 2004 LCD on with the wire.h libory Serial LCD Modul

// code stored in the sketch: AnalogReadSerial2LCD_LED.ino
#include <Wire.h>
#include <LiquidCrystal_I2C.h>

LiquidCrystal_I2C lcd(0x27, 16, 2);   // adress and format LCD

const int analogInPin = A0;           // Analog input pin that the potentiometer is attached to
const int analogOutPin = 9;           // Analog output pin that the LED is attached to

int sensorValue = 0;                  // value read from the pot
int outputValue = 0;                  // value output to the PWM (analog out)

void setup() {
  lcd.init();                         // init LCD
  lcd.backlight();
  lcd.home();
  lcd.setCursor(5, 0);                // place static text
  lcd.print("ADC = ");
  lcd.setCursor(15, 0);
  lcd.print("V");
  lcd.setCursor(0, 1);
  lcd.print("LED : ");
  lcd.setCursor(12, 1);
  lcd.print("%");
  Serial.begin(9600);                 // optional serial monitor
}

void loop() {
  int sensorValue = analogRead(analogInPin);          // read analog A0 en store in sensorValue
  float voltValue = 5.0 / 1024.0 * sensorValue;       // calculate volt at analog A0 and store in voltValue
  float percentValue = sensorValue / 1024.0 * 100.0;  // calculate percentage analog A0 and store in percentValue
  outputValue = map(sensorValue, 0, 1023, 0, 255);    // map analog input to analog output and store in outputValue
  analogWrite(analogOutPin, outputValue);             // write outputValue to analogOutPin

  lcd.setCursor(0, 0);                                // set cursor at deserid position
  leadingZeros(sensorValue, 4);                       // print sensorvalue with number of leading-characters (0 or space as specified in function leadingZeros)
  lcd.setCursor(10, 0);                               // set cursor at deserid position
  lcd.print(voltValue);                               // print voltValue
  lcd.setCursor(6, 1);                                // set cursor at deserid position
  lcd.print(percentValue);                            // print percentValue

  Serial.print("sensor = " );                         // print the results to the serial monitor:
  Serial.print(sensorValue);
  Serial.print("\t output = ");
  Serial.print(outputValue);
  Serial.print("\t procent = ");
  Serial.println(percentValue);

  delay(1000);                                        // set delay
}

void leadingZeros( int value, int width) {            // display result with leading characters
  char valueStr[6];                                   // large enough to hold an int
  itoa (value, valueStr, 10);                         // itoa converts int to string
  int len = strlen(valueStr);                         // calculate length of valueStr
  if (len < width) {
    len = width - len;
    while (len--)
      lcd.print(' ');                                 // for leading zeros place '0' between (), for leading spaces place ' ' between ()
  }
  lcd.print(valueStr);
}
