# Fritzing sketch Exo7 (saved by Fritzing 0.9.3b)
breadboards: 1

parts:
  Composant1 = Arduino Mega ADK (Rev3)
  IC1 = L293D [package=THT]
  hc-sr1 = hc-sr04
  hc-sr2 = hc-sr04
  M1 = DC Motor
  M2 = DC Motor

nets:
  N1: Composant1.A0, hc-sr1.Echo
  N2: Composant1.A1, hc-sr1.Trig
  N3: Composant1.A2, hc-sr2.Echo
  N4: Composant1.A3, hc-sr2.Trig
  GND: Composant1.GND, IC1.0V, hc-sr1.GND, hc-sr2.GND
  VCC: Composant1.5V, IC1.+Vmotor, IC1.+V, hc-sr1.VCC, hc-sr2.VCC
  N5: Composant1.D0/RX0, IC1.Enable_1
  N6: Composant1.D1/TX0, IC1.Enable_2
  N7: Composant1.D2_PWM, IC1.In_1
  N8: Composant1.D3_PWM, IC1.In_2
  N9: Composant1.D4_PWM, IC1.In_3
  N10: Composant1.D5_PWM, IC1.In_4
  N11: IC1.Out_1_(_Controlled_by_Enable_1_), M1.pin_2
  N12: IC1.Out_2_(_Controlled_by_Enable_1_), M1.pin_1
  N13: IC1.Out_3_(_Controlled_by_Enable_2_), M2.pin_1
  N14: IC1.Out_4_(_Controlled_by_Enable_2_), M2.pin_2
